# Fritzing sketch pc_f_compUnit (saved by Fritzing 0.9.3b)
breadboards: 2

parts:
  RPM-Unit = Arduino Uno (Rev3)
  IC1 = IC, DIP package, 16 pins [chip_label=RFID_RC522]
  IC2 = L293D [package=THT]
  M1 = DC Motor
  U1 = Optocoupler [package=THT]
  U2 = Optocoupler [package=THT]
  R1 = Resistor [tolerance=±5% resistance=220 package="1206 [SMD]"]
  R3 = Resistor [tolerance=±5% resistance=220 package="1206 [SMD]"]
  R4 = Resistor [tolerance=±5% resistance=220 package="1206 [SMD]"]
  R5 = Resistor [tolerance=±5% resistance=220 package="1206 [SMD]"]
  D1 = Diode [package=diode-hv]
  D2 = Diode [package=diode-hv]
  D3 = Diode [package=diode-hv]
  D4 = Diode [package=diode-hv]
  IC3 = L293D [package=THT]
  M2 = DC Motor
  U3 = Optocoupler [package=THT]
  U4 = Optocoupler [package=THT]
  R6 = Resistor [tolerance=±5% resistance=220 package="1206 [SMD]"]
  R7 = Resistor [tolerance=±5% resistance=220 package="1206 [SMD]"]
  R8 = Resistor [tolerance=±5% resistance=220 package="1206 [SMD]"]
  R9 = Resistor [tolerance=±5% resistance=220 package="1206 [SMD]"]
  D5 = Diode [package=diode-hv]
  D6 = Diode [package=diode-hv]
  D7 = Diode [package=diode-hv]
  D8 = Diode [package=diode-hv]
  Maluska1 = maluska dil miniaturrelais [part_number="DIL Mini RY" package=THT]
  MPX1 = MPX4250AP pressure sensor [part_number=MPX]
  LCD1 = LCD screen
  IC4 = IC, DIP package, 32 pins [chip_label=i2c-LCD-Module]
  Power_plug1 = Power plug

nets:
  N1: RPM-Unit.A0, MPX1.V_out
  N2: RPM-Unit.D8, U1.Pin_2
  N3: RPM-Unit.D9_PWM, IC1.pin6
  N4: RPM-Unit.D10_PWM/SS, IC1.pin5
  N5: RPM-Unit.D11_PWM/MOSI, IC1.pin4
  N6: RPM-Unit.D12/MISO, IC1.pin3
  N7: RPM-Unit.D13/SCK, IC1.pin2
  N8: RPM-Unit.GND, IC1.pin1, IC4.pin17
  N9: RPM-Unit.A4/SDA, IC4.pin32
  N10: RPM-Unit.A5/SCL, IC4.pin31
  N11: RPM-Unit.D4, Maluska1.1
  N12: RPM-Unit.D5_PWM, U4.Pin_2
  N13: RPM-Unit.D6_PWM, U3.Pin_2
  N14: RPM-Unit.D7, U2.Pin_2
  N15: RPM-Unit.3V3, IC1.pin16, IC2.+V, R1.Pin_0, R3.Pin_0, R4.Pin_0, R5.Pin_0, D1.C, D4.C, IC3.+V, R6.Pin_0, R7.Pin_0, R8.Pin_0, R9.Pin_0, D5.C, D7.C, IC4.pin18
  N16: IC2.In_1, U1.Pin_5, R3.Pin_1
  N17: IC2.Out_1_(_Controlled_by_Enable_1_), M1.pin_2, D2.C
  GND: IC2.0V, U1.Pin_4, U2.Pin_4, IC3.0V, U3.Pin_4, U4.Pin_4, Maluska1.16, MPX1.GND, Power_plug1.GND
  N18: IC2.Out_2_(_Controlled_by_Enable_1_), M1.pin_1, D3.C
  N19: IC2.In_2, U2.Pin_5, R5.Pin_1
  N20: IC2.+Vmotor, MPX1.Vs
  N21: U1.Pin_1, R1.Pin_1
  N22: U2.Pin_1, R4.Pin_1
  N23: IC3.In_1, U3.Pin_5, R7.Pin_1
  N24: IC3.Out_1_(_Controlled_by_Enable_1_), M2.pin_2, D8.C
  N25: IC3.Out_2_(_Controlled_by_Enable_1_), M2.pin_1, D6.C
  N26: IC3.In_2, U4.Pin_5, R8.Pin_1
  N27: IC3.+Vmotor, Power_plug1.VCC
  N28: U3.Pin_1, R6.Pin_1
  N29: U4.Pin_1, R9.Pin_1
  N30: LCD1.VSS, IC4.pin1
  N31: LCD1.VDD, IC4.pin2
  N32: LCD1.V0, IC4.pin3
  N33: LCD1.RS, IC4.pin4
  N34: LCD1.R/W, IC4.pin5
  N35: LCD1.E, IC4.pin6
  N36: LCD1.DB0, IC4.pin7
  N37: LCD1.DB1, IC4.pin8
  N38: LCD1.DB2, IC4.pin9
  N39: LCD1.DB3, IC4.pin10
  N40: LCD1.DB4, IC4.pin11
  N41: LCD1.DB5, IC4.pin12
  N42: LCD1.DB6, IC4.pin13
  N43: LCD1.DB7, IC4.pin14
  N44: LCD1.LED+, IC4.pin15
  N45: LCD1.LED-, IC4.pin16

notes:
  13 = SCK
  12 = MISO
  11 = MOSI
  10 = SDA
  9 = RST
  RFID-Reader
  Airlock
  Compressor
  Fan
