# Fritzing sketch pc_f_devA (saved by Fritzing 0.9.3b)

parts:
  Raspberry_Pi_1 = Raspberry Pi 3 [part_number=RPI-3-V1.2]
  LED1 = RGB LED (com. cathode, rbg) [package="5 mm [THT]"]

nets:
  N1: Raspberry_Pi_1.GIPO26, LED1.red_anode
  N2: Raspberry_Pi_1.GND, LED1.common_cathode
  N3: Raspberry_Pi_1.GIPO21, LED1.green_anode
  N4: Raspberry_Pi_1.GIPO20, LED1.blue_anode

notes:
  USB-Connection to Main-Unit
  USB-Connection to RPM-Unit
