# Fritzing sketch pc_f_devB (saved by Fritzing 0.9.3b)

parts:
  Raspberry_Pi_1 = Raspberry Pi 3 [part_number=RPI-3-V1.2]
  Maluska1 = maluska dil miniaturrelais [part_number="DIL Mini RY" package=THT]
  Maluska2 = maluska dil miniaturrelais [part_number="DIL Mini RY" package=THT]
  Maluska3 = maluska dil miniaturrelais [part_number="DIL Mini RY" package=THT]
  M1 = DC Motor
  Power_plug1 = Power plug
  LED1 = RGB LED (com. cathode, rbg) [package="5 mm [THT]"]
  M2 = DC Motor

nets:
  N1: Raspberry_Pi_1.GND, Maluska1.1, Maluska2.16, Maluska3.16, LED1.common_cathode
  N2: Raspberry_Pi_1.GIPO13, Maluska2.1, Maluska3.1
  N3: Raspberry_Pi_1.GIPO19, Maluska1.16
  N4: Raspberry_Pi_1.GIPO26, LED1.red_anode
  N5: Raspberry_Pi_1.GIPO21, LED1.green_anode
  N6: Raspberry_Pi_1.GIPO20, LED1.blue_anode
  N7: Maluska1.4, Maluska1.11, Power_plug1.GND
  N8: Maluska1.8, Maluska2.6
  N9: Maluska2.4, M1.pin_2, M2.pin_2
  N10: Maluska3.4, M1.pin_1
  N11: Maluska3.6, Power_plug1.VCC

notes:
  9V
