# Fritzing sketch pc_f_mainUnit (saved by Fritzing 0.9.3b)
breadboards: 2

parts:
  IC5 = IC, DIP package, 32 pins [chip_label="2.8\" TFT-Display + SD"]
  Bauteil1 = Arduino Mega 2560 (Rev3)
  DS1 = DS18B20 1-Wire Temperature Sensor [part_number=DS18B20]
  DS2 = DS18B20 1-Wire Temperature Sensor [part_number=DS18B20]
  RHT1 = Humidity and Temperature Sensor RHT03 [part_number=DHT11]
  U1 = ADXL345 [package=lga14]

nets:
  N1: IC5.pin7, Bauteil1.A0
  N2: IC5.pin8, Bauteil1.A1
  N3: IC5.pin9, Bauteil1.A2
  GND: IC5.pin16, Bauteil1.GND, DS1.GND, DS2.GND, RHT1.GND_1, U1.GND
  VDD: IC5.pin17, Bauteil1.5V, DS1.VDD, DS2.VDD, RHT1.Vcc, U1.VDD
  N4: IC5.pin23, Bauteil1.D2_PWM
  N5: IC5.pin24, Bauteil1.D3_PWM
  N6: IC5.pin25, Bauteil1.D4_PWM
  N7: IC5.pin26, Bauteil1.D5_PWM
  N8: IC5.pin27, Bauteil1.D6_PWM
  N9: IC5.pin28, Bauteil1.D7_PWM
  N10: IC5.pin29, Bauteil1.D8_PWM
  N11: IC5.pin30, Bauteil1.D9_PWM
  N12: IC5.pin31, Bauteil1.D10_PWM
  N13: IC5.pin32, Bauteil1.D11_PWM
  N14: Bauteil1.A15, RHT1.Data-signal
  N15: Bauteil1.D21/SCL, U1.SCL
  N16: Bauteil1.D20/SDA, U1.SDA
  N17: Bauteil1.D22, DS2.DQ
  N18: Bauteil1.D23, DS1.DQ

notes:
  USB-Connection to RPi Dev.A
