# Fritzing sketch pc_f_rpmUnit (saved by Fritzing 0.9.3b)

parts:
  RPM-Unit = Arduino Uno (Rev3)
  Photoresistor = PHOTOCELL [package=photocell-kit]
  IC5 = IC, DIP package, 32 pins [chip_label=i2c-LCD-Module]
  LCD2 = LCD screen
  LED1 = LED - 5mm [color="Red (633nm)" package="5 mm [THT]"]

nets:
  N1: RPM-Unit.A0, Photoresistor.P$1
  N2: RPM-Unit.D9_PWM, LED1.anode
  N3: RPM-Unit.GND, Photoresistor.P$2, IC5.pin17, LED1.cathode
  N4: RPM-Unit.A4/SDA, IC5.pin32
  N5: RPM-Unit.A5/SCL, IC5.pin31
  N6: RPM-Unit.3V3, IC5.pin18
  N7: IC5.pin1, LCD2.VSS
  N8: IC5.pin2, LCD2.VDD
  N9: IC5.pin3, LCD2.V0
  N10: IC5.pin4, LCD2.RS
  N11: IC5.pin5, LCD2.R/W
  N12: IC5.pin6, LCD2.E
  N13: IC5.pin7, LCD2.DB0
  N14: IC5.pin8, LCD2.DB1
  N15: IC5.pin9, LCD2.DB2
  N16: IC5.pin10, LCD2.DB3
  N17: IC5.pin11, LCD2.DB4
  N18: IC5.pin12, LCD2.DB5
  N19: IC5.pin13, LCD2.DB6
  N20: IC5.pin14, LCD2.DB7
  N21: IC5.pin15, LCD2.LED+
  N22: IC5.pin16, LCD2.LED-

notes:
  USB-Connection to RPi Dev.A
  Laseremitter
  Photoresistor
